// Digital circuit DMux8Way.dig as structural Verilog
module DMux8Way (
  input  in,
  input  [2:0] sel,
  output a,
  output b,
  output c,
  output d,
  output a_2,
  output b_2,
  output c_2,
  output d_2
);

  wire dmux4way_1_a, dmux4way_1_b, dmux4way_1_c, dmux4way_1_d;

  DMux4Way dmux4way_1 (.in(in), .sel(sel[2:1]), .a(dmux4way_1_a), .b(dmux4way_1_b), .c(dmux4way_1_c), .d(dmux4way_1_d));
  DeMux demux_1 (.in(dmux4way_1_a), .sel(sel[0]), .a(a), .b(b));
  DeMux demux_2 (.in(dmux4way_1_b), .sel(sel[0]), .a(c), .b(d));
  DeMux demux_3 (.in(dmux4way_1_c), .sel(sel[0]), .a(a_2), .b(b_2));
  DeMux demux_4 (.in(dmux4way_1_d), .sel(sel[0]), .a(c_2), .b(d_2));
endmodule
