// Digital circuit ALU.dig as structural Verilog
module ALU (
  input  [15:0] x,
  input  [15:0] y,
  input  zx,
  input  nx,
  input  zy,
  input  ny,
  input  f,
  input  no,
  output [15:0] out,
  output zr,
  output ng
);

  wire or16way_1_out;
  wire [15:0] add16_1_out, and16_1_out, mux16_1_out, mux16_2_out, mux16_3_out, mux16_4_out, mux16_5_out,
       not16_1_out, not16_2_out, not16_3_out;

  Mux16 mux16_1 (.a(x), .b({16{1'b0}}), .sel(zx), .out(mux16_1_out));
  Mux16 mux16_2 (.a(y), .b({16{1'b0}}), .sel(zy), .out(mux16_2_out));
  Not16 not16_1 (.in(mux16_1_out), .out(not16_1_out));
  Not16 not16_2 (.in(mux16_2_out), .out(not16_2_out));
  Mux16 mux16_3 (.a(mux16_1_out), .b(not16_1_out), .sel(nx), .out(mux16_3_out));
  Mux16 mux16_4 (.a(mux16_2_out), .b(not16_2_out), .sel(ny), .out(mux16_4_out));
  And16 and16_1 (.a(mux16_3_out), .b(mux16_4_out), .out(and16_1_out));
  Add16 add16_1 (.b(mux16_3_out), .a(mux16_4_out), .out(add16_1_out));
  Mux16 mux16_5 (.a(and16_1_out), .b(add16_1_out), .sel(f), .out(mux16_5_out));
  Not16 not16_3 (.in(mux16_5_out), .out(not16_3_out));
  Mux16 mux16_6 (.a(mux16_5_out), .b(not16_3_out), .sel(no), .out(out));
  Or16Way or16way_1 (.in(out), .out(or16way_1_out));
  IsNg16 isng16_1 (.in(out), .out(ng));
  Not not_1 (.in(or16way_1_out), .out(zr));
endmodule
