// Digital circuit Add16.dig as structural Verilog
module Add16 (
  input  [15:0] b,
  input  [15:0] a,
  output [15:0] out
);

  wire fulladder_2_carry, fulladder_3_carry, fulladder_4_carry, fulladder_5_carry, fulladder_6_carry,
       fulladder_7_carry, fulladder_8_carry, fulladder_9_carry, fulladder_10_carry, fulladder_11_carry,
       fulladder_12_carry, fulladder_13_carry, fulladder_14_carry, fulladder_15_carry, halfadder_1_carry;

  FullAdder fulladder_1 (.a(b[15]), .b(a[15]), .c(fulladder_2_carry), .sum(out[15]));  // open: carry
  FullAdder fulladder_2 (.a(b[14]), .b(a[14]), .c(fulladder_3_carry), .sum(out[14]), .carry(fulladder_2_carry));
  FullAdder fulladder_3 (.a(b[13]), .b(a[13]), .c(fulladder_4_carry), .sum(out[13]), .carry(fulladder_3_carry));
  FullAdder fulladder_4 (.a(b[12]), .b(a[12]), .c(fulladder_5_carry), .sum(out[12]), .carry(fulladder_4_carry));
  FullAdder fulladder_5 (.a(b[11]), .b(a[11]), .c(fulladder_6_carry), .sum(out[11]), .carry(fulladder_5_carry));
  FullAdder fulladder_6 (.a(b[10]), .b(a[10]), .c(fulladder_7_carry), .sum(out[10]), .carry(fulladder_6_carry));
  FullAdder fulladder_7 (.a(b[9]), .b(a[9]), .c(fulladder_8_carry), .sum(out[9]), .carry(fulladder_7_carry));
  FullAdder fulladder_8 (.a(b[8]), .b(a[8]), .c(fulladder_9_carry), .sum(out[8]), .carry(fulladder_8_carry));
  FullAdder fulladder_9 (.a(b[7]), .b(a[7]), .c(fulladder_10_carry), .sum(out[7]), .carry(fulladder_9_carry));
  FullAdder fulladder_10 (.a(b[6]), .b(a[6]), .c(fulladder_11_carry), .sum(out[6]), .carry(fulladder_10_carry));
  FullAdder fulladder_11 (.a(b[5]), .b(a[5]), .c(fulladder_12_carry), .sum(out[5]), .carry(fulladder_11_carry));
  FullAdder fulladder_12 (.a(b[4]), .b(a[4]), .c(fulladder_13_carry), .sum(out[4]), .carry(fulladder_12_carry));
  FullAdder fulladder_13 (.a(b[3]), .b(a[3]), .c(fulladder_14_carry), .sum(out[3]), .carry(fulladder_13_carry));
  FullAdder fulladder_14 (.a(b[2]), .b(a[2]), .c(fulladder_15_carry), .sum(out[2]), .carry(fulladder_14_carry));
  FullAdder fulladder_15 (.a(b[1]), .b(a[1]), .c(halfadder_1_carry), .sum(out[1]), .carry(fulladder_15_carry));
  HalfAdder halfadder_1 (.a(b[0]), .b(a[0]), .sum(out[0]), .carry(halfadder_1_carry));
endmodule
