// Digital circuit FullAdder.dig as structural Verilog
module FullAdder (
  input  a,
  input  b,
  input  c,
  output sum,
  output carry
);

  wire halfadder_1_carry, halfadder_1_sum, halfadder_2_carry;

  HalfAdder halfadder_1 (.a(a), .b(b), .sum(halfadder_1_sum), .carry(halfadder_1_carry));
  HalfAdder halfadder_2 (.a(c), .b(halfadder_1_sum), .sum(sum), .carry(halfadder_2_carry));
  Xor xor_1 (.a(halfadder_2_carry), .b(halfadder_1_carry), .out(carry));
endmodule
