// Digital circuit HalfAdder.dig as structural Verilog
module HalfAdder (
  input  a,
  input  b,
  output out,
  output carry
);

  Xor xor_1 (.a(a), .b(b), .out(out));
  And and_1 (.a(a), .b(b), .out(carry));
endmodule
