// Digital circuit DLatch.dig as structural Verilog
module DLatch (
  input  D,
  input  E,
  output Q
);

  wire and_1_out, and_2_out, nor_2_out, not_1_out;

  not not_1 (not_1_out, D);
  and and_1 (and_1_out, E, not_1_out);
  and and_2 (and_2_out, E, D);
  nor nor_1 (Q, and_1_out, nor_2_out);
  nor nor_2 (nor_2_out, Q, and_2_out);
endmodule
