// Digital circuit HalfAdder.dig as structural Verilog
module HalfAdder (
  input  a,
  input  b,
  output sum,
  output carry
);

  Xor xor_1 (.a(a), .b(b), .out(sum));
  And and_1 (.a(a), .b(b), .out(carry));
endmodule
