// Digital circuit Mux8Way16.dig as structural Verilog
module Mux8Way16 (
  input  [15:0] a,
  input  [15:0] b,
  input  [15:0] c,
  input  [15:0] d,
  input  [2:0] sel,
  input  [15:0] e,
  input  [15:0] f,
  input  [15:0] g,
  input  [15:0] h,
  output [15:0] out
);

  wire [15:0] mux4way16_1_out, mux4way16_2_out;

  Mux4Way16 mux4way16_1 (.a(a), .b(b), .c(c), .d(d), .sel(sel[1:0]), .out(mux4way16_1_out));
  Mux4Way16 mux4way16_2 (.a(e), .b(f), .c(g), .d(h), .sel(sel[1:0]), .out(mux4way16_2_out));
  Mux16 mux16_1 (.a(mux4way16_1_out), .b(mux4way16_2_out), .sel(sel[2]), .out(out));
endmodule
