// Digital circuit PC.dig as structural Verilog
module PC (
  input  [15:0] in,
  input  load,
  input  reset,
  input  CLK,
  input  inc,
  output [15:0] out
);

  wire [15:0] inc16_1_out, mux16_1_out, mux16_2_out, mux16_3_out;

  Mux16 mux16_1 (.a(out), .b(inc16_1_out), .sel(inc), .out(mux16_1_out));
  Mux16 mux16_2 (.a(mux16_1_out), .b(in), .sel(load), .out(mux16_2_out));
  Inc16 inc16_1 (.in(out), .out(inc16_1_out));
  Mux16 mux16_3 (.a(mux16_2_out), .b({16{1'b0}}), .sel(reset), .out(mux16_3_out));
  Register register_1 (.in(mux16_3_out), .load(1'b1), .CLK(CLK), .out(out));

  // Notes on the sheet:
  //   CLK: Hz: 10
endmodule
