// Digital circuit RAM64.dig as structural Verilog
module RAM64 (
  input  [15:0] in,
  input  load,
  input  [5:0] addr,
  input  CLK,
  output [15:0] out
);

  wire dmux8way_1_a, dmux8way_1_a_2, dmux8way_1_b, dmux8way_1_b_2, dmux8way_1_c, dmux8way_1_c_2,
       dmux8way_1_d, dmux8way_1_d_2;
  wire [15:0] ram8_1_out, ram8_2_out, ram8_3_out, ram8_4_out, ram8_5_out, ram8_6_out, ram8_7_out, ram8_8_out;

  DMux8Way dmux8way_1 (
    .in(load), .sel(addr[5:3]), .a(dmux8way_1_a), .b(dmux8way_1_b), .c(dmux8way_1_c), .d(dmux8way_1_d),
    .a_2(dmux8way_1_a_2), .b_2(dmux8way_1_b_2), .c_2(dmux8way_1_c_2), .d_2(dmux8way_1_d_2));
  RAM8 ram8_1 (.in(in), .load(dmux8way_1_a), .addr(addr[2:0]), .CLK(CLK), .out(ram8_1_out));
  RAM8 ram8_2 (.in(in), .load(dmux8way_1_b), .addr(addr[2:0]), .CLK(CLK), .out(ram8_2_out));
  RAM8 ram8_3 (.in(in), .load(dmux8way_1_c), .addr(addr[2:0]), .CLK(CLK), .out(ram8_3_out));
  RAM8 ram8_4 (.in(in), .load(dmux8way_1_d), .addr(addr[2:0]), .CLK(CLK), .out(ram8_4_out));
  RAM8 ram8_5 (.in(in), .load(dmux8way_1_a_2), .addr(addr[2:0]), .CLK(CLK), .out(ram8_5_out));
  RAM8 ram8_6 (.in(in), .load(dmux8way_1_b_2), .addr(addr[2:0]), .CLK(CLK), .out(ram8_6_out));
  RAM8 ram8_7 (.in(in), .load(dmux8way_1_c_2), .addr(addr[2:0]), .CLK(CLK), .out(ram8_7_out));
  RAM8 ram8_8 (.in(in), .load(dmux8way_1_d_2), .addr(addr[2:0]), .CLK(CLK), .out(ram8_8_out));
  Mux8Way16 mux8way16_1 (
    .a(ram8_1_out), .b(ram8_2_out), .c(ram8_3_out), .d(ram8_4_out), .sel(addr[5:3]), .e(ram8_5_out),
    .f(ram8_6_out), .g(ram8_7_out), .h(ram8_8_out), .out(out));

  // Notes on the sheet:
  //   CLK: Hz: 10
endmodule
