// Digital circuit DMux4Way.dig as structural Verilog
module DMux4Way (
  input  in,
  input  [1:0] sel,
  output a,
  output b,
  output c,
  output d
);

  wire demux_1_a, demux_1_b;

  DeMux demux_1 (.in(in), .sel(sel[0]), .a(demux_1_a), .b(demux_1_b));
  DeMux demux_2 (.in(demux_1_a), .sel(sel[1]), .a(a), .b(c));
  DeMux demux_3 (.in(demux_1_b), .sel(sel[1]), .a(b), .b(d));
endmodule
