// Digital circuit RAM8.dig as structural Verilog
module RAM8 (
  input  [15:0] in,
  input  load,
  input  [2:0] addr,
  input  CLK,
  output [15:0] out
);

  wire dmux8way_1_a, dmux8way_1_a_2, dmux8way_1_b, dmux8way_1_b_2, dmux8way_1_c, dmux8way_1_c_2,
       dmux8way_1_d, dmux8way_1_d_2;
  wire [15:0] register_1_out, register_2_out, register_3_out, register_4_out, register_5_out, register_6_out,
       register_7_out, register_8_out;

  DMux8Way dmux8way_1 (
    .in(load), .sel(addr), .a(dmux8way_1_a), .b(dmux8way_1_b), .c(dmux8way_1_c), .d(dmux8way_1_d),
    .a_2(dmux8way_1_a_2), .b_2(dmux8way_1_b_2), .c_2(dmux8way_1_c_2), .d_2(dmux8way_1_d_2));
  Register register_1 (.in(in), .load(dmux8way_1_a), .CLK(CLK), .out(register_1_out));
  Register register_2 (.in(in), .load(dmux8way_1_b), .CLK(CLK), .out(register_2_out));
  Register register_3 (.in(in), .load(dmux8way_1_c), .CLK(CLK), .out(register_3_out));
  Register register_4 (.in(in), .load(dmux8way_1_d), .CLK(CLK), .out(register_4_out));
  Register register_5 (.in(in), .load(dmux8way_1_a_2), .CLK(CLK), .out(register_5_out));
  Register register_6 (.in(in), .load(dmux8way_1_b_2), .CLK(CLK), .out(register_6_out));
  Register register_7 (.in(in), .load(dmux8way_1_c_2), .CLK(CLK), .out(register_7_out));
  Register register_8 (.in(in), .load(dmux8way_1_d_2), .CLK(CLK), .out(register_8_out));
  Mux8Way16 mux8way16_1 (
    .a(register_1_out), .b(register_2_out), .c(register_3_out), .d(register_4_out), .sel(addr),
    .e(register_5_out), .f(register_6_out), .g(register_7_out), .h(register_8_out), .out(out));

  // Notes on the sheet:
  //   CLK: Hz: 10
endmodule
