// Digital circuit RAM512.dig as structural Verilog
module RAM512 (
  input  [15:0] in,
  input  load,
  input  [8:0] addr,
  input  CLK,
  output [15:0] out
);

  wire dmux8way_1_a, dmux8way_1_a_2, dmux8way_1_b, dmux8way_1_b_2, dmux8way_1_c, dmux8way_1_c_2,
       dmux8way_1_d, dmux8way_1_d_2;
  wire [15:0] ram64_1_out, ram64_2_out, ram64_3_out, ram64_4_out, ram64_5_out, ram64_6_out, ram64_7_out,
       ram64_8_out;

  DMux8Way dmux8way_1 (
    .in(load), .sel(addr[8:6]), .a(dmux8way_1_a), .b(dmux8way_1_b), .c(dmux8way_1_c), .d(dmux8way_1_d),
    .a_2(dmux8way_1_a_2), .b_2(dmux8way_1_b_2), .c_2(dmux8way_1_c_2), .d_2(dmux8way_1_d_2));
  RAM64 ram64_1 (.in(in), .load(dmux8way_1_a), .addr(addr[5:0]), .CLK(CLK), .out(ram64_1_out));
  RAM64 ram64_2 (.in(in), .load(dmux8way_1_b), .addr(addr[5:0]), .CLK(CLK), .out(ram64_2_out));
  RAM64 ram64_3 (.in(in), .load(dmux8way_1_c), .addr(addr[5:0]), .CLK(CLK), .out(ram64_3_out));
  RAM64 ram64_4 (.in(in), .load(dmux8way_1_d), .addr(addr[5:0]), .CLK(CLK), .out(ram64_4_out));
  RAM64 ram64_5 (.in(in), .load(dmux8way_1_a_2), .addr(addr[5:0]), .CLK(CLK), .out(ram64_5_out));
  RAM64 ram64_6 (.in(in), .load(dmux8way_1_b_2), .addr(addr[5:0]), .CLK(CLK), .out(ram64_6_out));
  RAM64 ram64_7 (.in(in), .load(dmux8way_1_c_2), .addr(addr[5:0]), .CLK(CLK), .out(ram64_7_out));
  RAM64 ram64_8 (.in(in), .load(dmux8way_1_d_2), .addr(addr[5:0]), .CLK(CLK), .out(ram64_8_out));
  Mux8Way16 mux8way16_1 (
    .a(ram64_1_out), .b(ram64_2_out), .c(ram64_3_out), .d(ram64_4_out), .sel(addr[8:6]), .e(ram64_5_out),
    .f(ram64_6_out), .g(ram64_7_out), .h(ram64_8_out), .out(out));

  // Notes on the sheet:
  //   CLK: Hz: 10
endmodule
