// Digital circuit Bit.dig as structural Verilog
module Bit (
  input  in,
  input  load,
  input  CLK,
  output out
);

  wire mux_1_out;

  Mux mux_1 (.a(out), .b(in), .sel(load), .out(mux_1_out));
  DFF dff_1 (.D(mux_1_out), .E(CLK), .out(out));

  // Notes on the sheet:
  //   CLK: Hz: 10
endmodule
