// Digital circuit DFF.dig as structural Verilog
module DFF (
  input  D,
  input  E,
  output out
);

  wire dlatch_1_q, not_1_out;

  not not_1 (not_1_out, E);
  DLatch dlatch_1 (.D(D), .E(not_1_out), .Q(dlatch_1_q));
  DLatch dlatch_2 (.D(dlatch_1_q), .E(E), .Q(out));
endmodule
