// Digital circuit Or16Way.dig as structural Verilog
module Or16Way (
  input  [15:0] in,
  output out
);

  wire or8way_1_out, or8way_2_out;

  Or8Way or8way_1 (.in(in[7:0]), .out(or8way_1_out));
  Or8Way or8way_2 (.in(in[15:8]), .out(or8way_2_out));
  Or or_1 (.a(or8way_1_out), .b(or8way_2_out), .out(out));
endmodule
