// Digital circuit Or8Way.dig as structural Verilog
module Or8Way (
  input  [7:0] in,
  output out
);

  wire or_1_out, or_2_out, or_3_out, or_4_out, or_5_out, or_6_out;

  or or_1 (or_1_out, in[0], in[1]);
  or or_2 (or_2_out, in[2], in[3]);
  or or_3 (or_3_out, in[4], in[5]);
  or or_4 (or_4_out, in[6], in[7]);
  or or_5 (or_5_out, or_1_out, or_2_out);
  or or_6 (or_6_out, or_3_out, or_4_out);
  or or_7 (out, or_5_out, or_6_out);
endmodule
