// Digital circuit RAM16K.dig as structural Verilog
module RAM16K (
  input  [15:0] in,
  input  load,
  input  [13:0] addr,
  input  CLK,
  output [15:0] out
);

  wire dmux4way_1_a, dmux4way_1_b, dmux4way_1_c, dmux4way_1_d;
  wire [15:0] ram4k_1_out, ram4k_2_out, ram4k_3_out, ram4k_4_out;

  DMux4Way dmux4way_1 (
    .in(load), .sel(addr[13:12]), .a(dmux4way_1_a), .b(dmux4way_1_b), .c(dmux4way_1_c), .d(dmux4way_1_d));
  RAM4K ram4k_1 (.in(in), .load(dmux4way_1_a), .addr(addr[11:0]), .CLK(CLK), .out(ram4k_1_out));
  RAM4K ram4k_2 (.in(in), .load(dmux4way_1_b), .addr(addr[11:0]), .CLK(CLK), .out(ram4k_2_out));
  RAM4K ram4k_3 (.in(in), .load(dmux4way_1_c), .addr(addr[11:0]), .CLK(CLK), .out(ram4k_3_out));
  RAM4K ram4k_4 (.in(in), .load(dmux4way_1_d), .addr(addr[11:0]), .CLK(CLK), .out(ram4k_4_out));
  Mux4Way16 mux4way16_1 (
    .a(ram4k_1_out), .b(ram4k_2_out), .c(ram4k_3_out), .d(ram4k_4_out), .sel(addr[13:12]), .out(out));

  // Notes on the sheet:
  //   CLK: Hz: 10
endmodule
