// Digital circuit RAM4K.dig as structural Verilog
module RAM4K (
  input  [15:0] in,
  input  load,
  input  [11:0] addr,
  input  CLK,
  output [15:0] out
);

  wire dmux8way_1_a, dmux8way_1_b, dmux8way_1_c, dmux8way_1_d, dmux8way_1_e, dmux8way_1_f, dmux8way_1_g,
       dmux8way_1_h;
  wire [15:0] ram512_1_out, ram512_2_out, ram512_3_out, ram512_4_out, ram512_5_out, ram512_6_out,
       ram512_7_out, ram512_8_out;

  DMux8Way dmux8way_1 (
    .in(load), .sel(addr[11:9]), .a(dmux8way_1_a), .b(dmux8way_1_b), .c(dmux8way_1_c), .d(dmux8way_1_d),
    .e(dmux8way_1_e), .f(dmux8way_1_f), .g(dmux8way_1_g), .h(dmux8way_1_h));
  RAM512 ram512_1 (.in(in), .load(dmux8way_1_a), .addr(addr[8:0]), .CLK(CLK), .out(ram512_1_out));
  RAM512 ram512_2 (.in(in), .load(dmux8way_1_b), .addr(addr[8:0]), .CLK(CLK), .out(ram512_2_out));
  RAM512 ram512_3 (.in(in), .load(dmux8way_1_c), .addr(addr[8:0]), .CLK(CLK), .out(ram512_3_out));
  RAM512 ram512_4 (.in(in), .load(dmux8way_1_d), .addr(addr[8:0]), .CLK(CLK), .out(ram512_4_out));
  RAM512 ram512_5 (.in(in), .load(dmux8way_1_e), .addr(addr[8:0]), .CLK(CLK), .out(ram512_5_out));
  RAM512 ram512_6 (.in(in), .load(dmux8way_1_f), .addr(addr[8:0]), .CLK(CLK), .out(ram512_6_out));
  RAM512 ram512_7 (.in(in), .load(dmux8way_1_g), .addr(addr[8:0]), .CLK(CLK), .out(ram512_7_out));
  RAM512 ram512_8 (.in(in), .load(dmux8way_1_h), .addr(addr[8:0]), .CLK(CLK), .out(ram512_8_out));
  Mux8Way16 mux8way16_1 (
    .a(ram512_1_out), .b(ram512_2_out), .c(ram512_3_out), .d(ram512_4_out), .sel(addr[11:9]),
    .e(ram512_5_out), .f(ram512_6_out), .g(ram512_7_out), .h(ram512_8_out), .out(out));

  // Notes on the sheet:
  //   CLK: Hz: 10
endmodule
