// Digital circuit CPU.dig as structural Verilog
module CPU (
  input  [15:0] inM,
  input  CLK,
  input  [15:0] instruction,
  input  reset,
  output [14:0] pc,
  output writeM,
  output [14:0] addressM,
  output [15:0] outM
);

  wire and_1_out, and_2_out, ge_out, gt_out, j1_out, j2_out, j3_out, jeq_out, jgt_out, jlt_out, jltjeq_out,
       jmp_out, ne_out, ng, not_1_out, not_2_out, or_1_out, zr;
  wire [15:0] D_register_out, mux16_1_out, mux16_2_out;
  wire [15:15] A_register_out, PC_out;

  not not_1 (not_1_out, instruction[15]);
  not not_2 (not_2_out, not_1_out);
  And and_1 (.a(not_2_out), .b(instruction[5]), .out(and_1_out));
  And j1 (.a(not_2_out), .b(instruction[2]), .out(j1_out));
  And j2 (.a(not_2_out), .b(instruction[1]), .out(j2_out));
  And j3 (.a(not_2_out), .b(instruction[0]), .out(j3_out));
  Mux16 mux16_1 (.a(instruction), .b(outM), .sel(not_2_out), .out(mux16_1_out));
  Or or_1 (.a(and_1_out), .b(not_1_out), .out(or_1_out));
  Not ge (.in(ng), .out(ge_out));
  And jlt (.a(ng), .b(j1_out), .out(jlt_out));
  Not ne (.in(zr), .out(ne_out));
  And jeq (.a(zr), .b(j2_out), .out(jeq_out));
  And gt (.a(ge_out), .b(ne_out), .out(gt_out));
  Register A_register (.in(mux16_1_out), .load(or_1_out), .CLK(CLK), .out({A_register_out[15], addressM}));
  Or jltjeq (.a(jlt_out), .b(jeq_out), .out(jltjeq_out));
  And jgt (.a(gt_out), .b(j3_out), .out(jgt_out));
  Or jmp (.a(jltjeq_out), .b(jgt_out), .out(jmp_out));
  And and_2 (.a(not_1_out), .b(instruction[4]), .out(and_2_out));
  Register D_register (.in(outM), .load(and_2_out), .CLK(CLK), .out(D_register_out));
  PC u_PC (
    .in({A_register_out[15], addressM}), .load(jmp_out), .reset(reset), .CLK(CLK), .inc(1'b1),
    .out({PC_out[15], pc}));
  Mux16 mux16_2 (.a({A_register_out[15], addressM}), .b(inM), .sel(instruction[12]), .out(mux16_2_out));
  ALU alu_1 ();
  And and_3 (.a(not_2_out), .b(instruction[3]), .out(writeM));

  // Other names for the same wires on the sheet: js[2:0] = instruction[2:0]; ds[2:0] = instruction[5:3];
  //   cs[5:0] = instruction[11:6]; no = instruction[6]; f = instruction[7]; ny = instruction[8]; zy = instruction[9];
  //   nx = instruction[10]; zx = instruction[11]; a = instruction[12]; ins = instruction[15]

  // Notes on the sheet:
  //   CLK: Hz: 10
endmodule
