// Digital circuit CPU.dig as structural Verilog
module CPU (
  input  [15:0] inM,
  input  CLK,
  input  [15:0] instruction,
  input  reset,
  output [14:0] pc,
  output writeM,
  output [14:0] addressM,
  output [15:0] outM
);

  wire and_1_out, and_2_out, and_3_out, and_4_out, and_5_out, and_6_out, and_7_out, and_8_out, and_9_out, ng,
       not_1_out, not_2_out, not_3_out, not_4_out, or_1_out, or_2_out, or_3_out, zr;
  wire [15:0] multiplexer_1_out, multiplexer_2_out, register_2_q;
  wire [15:15] PC_out, register_1_q;

  not not_1 (not_1_out, instruction[15]);
  not not_2 (not_2_out, not_1_out);
  and and_1 (and_1_out, not_2_out, instruction[5]);
  and and_2 (and_2_out, not_2_out, instruction[2]);
  and and_3 (and_3_out, not_2_out, instruction[1]);
  and and_4 (and_4_out, not_2_out, instruction[0]);
  Multiplexer #(.Bits(16)) multiplexer_1 (.sel(not_2_out), .in_0(instruction), .in_1(outM), .out(multiplexer_1_out));
  or or_1 (or_1_out, and_1_out, not_1_out);
  not not_3 (not_3_out, ng);
  and and_5 (and_5_out, ng, and_2_out);
  not not_4 (not_4_out, zr);
  and and_6 (and_6_out, zr, and_3_out);
  and and_7 (and_7_out, not_3_out, not_4_out);
  Register #(.Bits(16)) register_1 (.D(multiplexer_1_out), .C(CLK), .en(or_1_out), .Q({register_1_q[15], addressM}));
  or or_2 (or_2_out, and_5_out, and_6_out);
  and and_8 (and_8_out, and_7_out, and_4_out);
  or or_3 (or_3_out, or_2_out, and_8_out);
  and and_9 (and_9_out, not_1_out, instruction[4]);
  PC u_PC (
    .in({register_1_q[15], addressM}), .load(or_3_out), .reset(reset), .CLK(CLK), .inc(1'b1),
    .out({PC_out[15], pc}));
  Register #(.Bits(16)) register_2 (.D(outM), .C(CLK), .en(and_9_out), .Q(register_2_q));
  Multiplexer #(.Bits(16)) multiplexer_2 (
    .sel(instruction[12]), .in_0({register_1_q[15], addressM}), .in_1(inM), .out(multiplexer_2_out));
  ALU alu_1 ();
  and and_10 (writeM, not_2_out, instruction[3]);

  // Other names for the same wires on the sheet: js[2:0] = instruction[2:0]; ds[2:0] = instruction[5:3];
  //   cs[5:0] = instruction[11:6]; no = instruction[6]; f = instruction[7]; ny = instruction[8]; zy = instruction[9];
  //   nx = instruction[10]; zx = instruction[11]; a = instruction[12]; ins = instruction[15]

  // Notes on the sheet:
  //   CLK: Hz: 10
endmodule
