// Digital circuit Computer.dig as structural Verilog
module Computer (
  input  reset,
  input  CLK
);

  wire [14:0] undriven;
  wire [15:0] rom_1_d;

  ROM #(.AddrBits(15), .Bits(16)) rom_1 (.A(undriven), .sel(1'b1), .D(rom_1_d));
  CPU cpu_1 ();
  Memory memory_1 ();

  // Notes on the sheet:
  //   CLK: Hz: 10
  //   contents of rom_1 (hex, n*v repeats v):
  //   11,ec10,0,e308
endmodule
