// Digital circuit Memory.dig as structural Verilog
module Memory (
  input  [15:0] in,
  input  [14:0] address,
  input  load,
  input  CLK,
  output [15:0] out
);

  wire demultiplexer_1_out_0, demultiplexer_1_out_1, demultiplexer_1_out_2, demultiplexer_1_out_3, or_1_out;
  wire [15:0] Keyboard_q, RAM16K_d, Screen_d;

  Demultiplexer #(.Selector_Bits(2)) demultiplexer_1 (
    .sel(address[14:13]), .in(load), .out_0(demultiplexer_1_out_0), .out_1(demultiplexer_1_out_1),
    .out_2(demultiplexer_1_out_2), .out_3(demultiplexer_1_out_3));
  or or_1 (or_1_out, demultiplexer_1_out_0, demultiplexer_1_out_1);
  BlockRAMDualPort #(.AddrBits(14), .Bits(16)) RAM16K (
    .A(address[13:0]), .Din(in), .str(or_1_out), .C(CLK), .D(RAM16K_d));
  BlockRAMDualPort #(.AddrBits(13), .Bits(16)) Screen (
    .A(address[12:0]), .Din(in), .str(demultiplexer_1_out_2), .C(CLK), .D(Screen_d));
  Register #(.Bits(16)) Keyboard (.D(in), .C(CLK), .en(demultiplexer_1_out_3), .Q(Keyboard_q));
  Multiplexer #(.Selector_Bits(2), .Bits(16)) multiplexer_1 (
    .sel(address[14:13]), .in_0(RAM16K_d), .in_1(RAM16K_d), .in_2(Screen_d), .in_3(Keyboard_q), .out(out));

  // Other names for the same wires on the sheet: RAMAddr[13:0] = address[13:0]; ScreenAddr[12:0] = address[12:0];
  //   SignalBits[1:0] = address[14:13]

  // Notes on the sheet:
  //   CLK: Hz: 10
endmodule
