// Digital circuit PC.dig as structural Verilog
module PC (
  input  [15:0] in,
  input  load,
  input  reset,
  input  CLK,
  input  inc,
  output [15:0] out
);

  wire [15:0] inc16_1_out, multiplexer_1_out, multiplexer_2_out, multiplexer_3_out;

  Multiplexer #(.Bits(16)) multiplexer_1 (.sel(inc), .in_0(out), .in_1(inc16_1_out), .out(multiplexer_1_out));
  Multiplexer #(.Bits(16)) multiplexer_2 (.sel(load), .in_0(multiplexer_1_out), .in_1(in), .out(multiplexer_2_out));
  Inc16 inc16_1 (.in(out), .out(inc16_1_out));
  Multiplexer #(.Bits(16)) multiplexer_3 (
    .sel(reset), .in_0(multiplexer_2_out), .in_1({16{1'b0}}), .out(multiplexer_3_out));
  Register #(.Bits(16)) register_1 (.D(multiplexer_3_out), .C(CLK), .en(1'b1), .Q(out));

  // Notes on the sheet:
  //   CLK: Hz: 10
endmodule
