// Digital circuit ROM.dig as structural Verilog
module ROM (
  input  [14:0] address,
  output [15:0] out
);

  ROM #(.AddrBits(15), .Bits(16)) rom_1 (.A(address), .sel(1'b1), .D(out));

  // Notes on the sheet:
  //   contents of rom_1 (hex, n*v repeats v):
  //   0,1,2,3,4,5,6,7,8,9,a,b,c,d,e,f
endmodule
