// Digital circuit Computer.dig as structural Verilog
module Computer (
  input  reset,
  input  CLK
);

  wire [14:0] undriven;
  wire [15:0] rom_1_out;

  ROM rom_1 (.address(undriven), .out(rom_1_out));
  CPU cpu_1 ();
  Memory memory_1 ();

  // Notes on the sheet:
  //   CLK: Hz: 10
endmodule
