// Digital circuit Memory.dig as structural Verilog
module Memory (
  input  [15:0] in,
  input  [14:0] address,
  input  load,
  input  CLK,
  output [15:0] out
);

  wire dmux4way_1_a, dmux4way_1_b, dmux4way_1_c, dmux4way_1_d, or_1_out;
  wire [15:0] ram16k_1_out, register_1_out, Screen_p5;

  DMux4Way dmux4way_1 (
    .in(load), .sel(address[14:13]), .a(dmux4way_1_a), .b(dmux4way_1_b), .c(dmux4way_1_c), .d(dmux4way_1_d));
  Or or_1 (.a(dmux4way_1_a), .b(dmux4way_1_b), .out(or_1_out));
  RAM16K ram16k_1 (.in(in), .load(or_1_out), .addr(address[13:0]), .CLK(CLK), .out(ram16k_1_out));
  // RAM8 Screen: pin names not known; wires that end beside it: in, dmux4way_1_c, address[12:0], CLK, Screen_p5
  Register register_1 (.in(in), .load(dmux4way_1_d), .CLK(CLK), .out(register_1_out));
  Mux4Way16 mux4way16_1 (
    .a(ram16k_1_out), .b(ram16k_1_out), .c(Screen_p5), .d(register_1_out), .sel(address[14:13]), .out(out));

  // Other names for the same wires on the sheet: RAMAddr[13:0] = address[13:0]; ScreenAddr[12:0] = address[12:0];
  //   SignalBits[1:0] = address[14:13]

  // Notes on the sheet:
  //   CLK: Hz: 10
endmodule
