// Digital circuit ROM32K.dig as structural Verilog
module ROM32K (
  input  [14:0] A,
  input  sel,
  output [15:0] D
);

  ROM #(.AddrBits(15), .Bits(16)) ROM32K (.A(A), .sel(sel), .D(D));

  // Notes on the sheet:
  //   contents of ROM32K (hex, n*v repeats v):
  //   0,1,2,3,4,5,6,7,8,9,a,b,c,d,e,f
endmodule
