// Digital circuit sketch.dig as structural Verilog
module sketch (
  input  [15:0] a,
  input  [15:0] b,
  input  sel,
  output [15:0] out_4
);

  Mux mux_1 (.a(a[0]), .b(b[0]), .sel(sel), .out(out_4[0]));
  Mux mux_2 (.a(a[1]), .b(b[1]), .sel(sel), .out(out_4[1]));
  Mux mux_3 (.a(a[2]), .b(b[2]), .sel(sel), .out(out_4[2]));
  Mux mux_4 (.a(a[3]), .b(b[3]), .sel(sel), .out(out_4[3]));
  Mux mux_5 (.a(a[4]), .b(b[4]), .sel(sel), .out(out_4[4]));
  Mux mux_6 (.a(a[5]), .b(b[5]), .sel(sel), .out(out_4[5]));
  Mux mux_7 (.a(a[6]), .b(b[6]), .sel(sel), .out(out_4[6]));
  Mux mux_8 (.a(a[7]), .b(b[7]), .sel(sel), .out(out_4[7]));
  Mux mux_9 (.a(a[8]), .b(b[8]), .sel(sel), .out(out_4[8]));
  Mux mux_10 (.a(a[9]), .b(b[9]), .sel(sel), .out(out_4[9]));
  Mux mux_11 (.a(a[10]), .b(b[10]), .sel(sel), .out(out_4[10]));
  Mux mux_12 (.a(a[11]), .b(b[11]), .sel(sel), .out(out_4[11]));
  Mux mux_13 (.a(a[12]), .b(b[12]), .sel(sel), .out(out_4[12]));
  Mux mux_14 (.a(a[13]), .b(b[13]), .sel(sel), .out(out_4[13]));
  Mux mux_15 (.a(a[14]), .b(b[14]), .sel(sel), .out(out_4[14]));
  Mux mux_16 (.a(a[15]), .b(b[15]), .sel(sel), .out(out_4[15]));

  // Other names for the same wires on the sheet: out0 = out_4[0]; out1 = out_4[1]; out2 = out_4[2]; out3 = out_4[3];
  //   out4 = out_4[4]; out5 = out_4[5]; out6 = out_4[6]; out7 = out_4[7]; out8 = out_4[8]; out9 = out_4[9];
  //   out10 = out_4[10]; out11 = out_4[11]; out12 = out_4[12]; out13 = out_4[13]; out14 = out_4[14];
  //   out15 = out_4[15]; s = sel
endmodule
